# Fritzing sketch Circuit (saved by Fritzing 0.9.3b)
breadboards: 1

parts:
  U1 = TLP621 [package=THT]
  R1 = Resistor [tolerance=±5% resistance=220 package=THT]

nets:
  N1: U1.Pin_4, R1.Pin_0
  GND: U1.Pin_3
